# Fritzing sketch Controle Portão Eletrônico com App (saved by Fritzing 0.9.3b)
breadboards: 1

parts:
  Q1 = NPN-Transistor [package="TO92 [THT]"]
  R1 = Resistor [tolerance=±5% resistance=10k package=THT]
  HC-06_3V3 = Bluetooth HC-05 Macho
  D1 = Zener Diode [part_number=1N4732A breakdown_voltage=3.6V package="Melf DO-213 AB [SMD]"]
  U1 = RELAY-2 [package=relay-g5v]
  SW_CLOSED = Reed switch [package=THT]
  R2 = Resistor [tolerance=±5% resistance=470 package=THT]
  R3 = Resistor [tolerance=±5% resistance=10k package=THT]
  Q2 = PNP-Transistor [package="TO92 [THT]"]
  R4 = Resistor [tolerance=±5% resistance=330 package=THT]

nets:
  GND: Q1.E, HC-06_3V3.GND, D1.anode, SW_CLOSED.pin_1
  N1: Q1.B, R1.Pin_1
  N2: Q1.C, U1.9
  Arduino relay - 3: R1.Pin_0
  N3: HC-06_3V3.TXD, D1.cathode, R2.Pin_0
  Arduino SoftSerial RX - 11: HC-06_3V3.RXD
  N4: HC-06_3V3.VCC, Q2.C
  12V: U1.2
  BOTOEIRA 0: U1.6
  BOTOEIRA 1: U1.10
  Arduino sw_closed - 6: SW_CLOSED.pin_2, R3.Pin_0
  Arduino SoftSerial TX - 10: R2.Pin_1
  5V: R3.Pin_1
  3.3V: Q2.E
  N5: Q2.B, R4.Pin_1
  Arduino bt_disable - 9: R4.Pin_0

notes:
  Parte da Placa do Portão MX-30
  Reset no bluetooth pode resolver problemas de conexão
